# Fritzing sketch SD_transmit (saved by Fritzing 0.9.3b)

parts:
  Part4 = Arduino Uno (Rev3) - ICSP
  Part5 = Adafruit Ultimate GPS Logger Shield [part_number="Adafruit #1272"]
  Part6 = Bluetooth Module Breakout - Roving Networks (RN-41)

nets:
  N1: Part4.A0, Part5.A0
  N2: Part4.A1, Part5.A1
  N3: Part4.A2, Part5.A2
  N4: Part4.A3, Part5.A3
  N5: Part4.A4/SDA, Part5.A4, Part5.SDA
  N6: Part4.A5/SCL, Part5.A5, Part5.SCL
  5V: Part4.5V, Part5.+5V
  N7: Part4.RESET, Part5.RESET
  GND: Part4.GND, Part5.GND
  N8: Part4.D8, Part4.D7, Part5.D7, Part5.D8
  N9: Part4.D9_PWM, Part5.D9
  N10: Part4.D10_PWM/SS, Part5.SD_CS
  N11: Part4.D11_PWM/MOSI, Part5.MOSI
  N12: Part4.D12/MISO, Part5.MISO
  N13: Part4.D13/SCK, Part5.SCK
  N14: Part4.AREF, Part5.AREF
  N15: Part4.D0/RX, Part5.D0
  N16: Part4.D1/TX, Part5.D1
  N17: Part4.D2, Part5.D2
  N18: Part4.D3_PWM, Part5.D3
  N19: Part4.D4, Part5.D4
  N20: Part4.D5_PWM, Part5.D5
  N21: Part4.D6_PWM, Part5.D6
  N22: Part4.IOREF, Part5.IOREF
  N23: Part4.3V3, Part5.3V
  VIN: Part4.VIN, Part5.VIN
  N24: Part4.N/C, Part5.NC
  N25: Part5.N$17, Part6.PIO3
  N26: Part5.N$18, Part6.PIO5
  N27: Part5.N$19, Part6.UARTCTS
  N28: Part5.N$20, Part6.SPICSB
  N29: Part5.N$23, Part6.PIO2
  N30: Part5.N$41, Part6.GND
  N31: Part5.N$51, Part6.UARTTX
  N32: Part5.N$54, Part6.10
  N33: Part5.N$63, Part6.PIO4
  N34: Part5.N$74, Part6.UARTRTS
  N35: Part5.N$102, Part6.PIO11
  N36: Part5.N$103, Part6.PIO10
  N37: Part5.N$104, Part6.SPIMOSI
  N38: Part5.N$105, Part6.PIO6
  N39: Part5.N$106, Part6.PIO7
  N40: Part5.N$107, Part6.SPICLK
  N41: Part5.N$109, Part6.RESET
  N42: Part5.N$118, Part6.SPIMISO
  N43: Part5.N$163, Part6.VCC
  N44: Part5.N$173, Part6.UARTRX

custom parts:
  Adafruit Ultimate GPS Logger Shield: Brand new and better than ever, we've replaced our Adafruit GPS shield kit with this assembled shield that comes with an Ultimate GPS module. This GPS shield works great with either UNO or Leonardo Arduinos and is designed to log data to an SD card. Or you can leave the SD card out and use the GPS for a geocaching project, or maybe a music player that changes tunes depending on where you are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
